// Logisim project evolution_D_FF.circ as structural Verilog: 1 circuit, main circuit main
module main (
  input  preset,
  input  reset,
  input  enable,
  input  set,
  input  clear
);

  wire and_1_out, and_2_out, and_3_out, and_4_out, and_5_out, not_1_out, not_2_out, not_3_out, or_1_out,
       or_2_out, or_3_out;

  and and_1 (and_1_out, reset, enable);
  and and_2 (and_2_out, enable, set);
  not not_1 (not_1_out, and_1_out);
  or or_1 (or_1_out, and_2_out, and_5_out);
  or or_2 (or_2_out, preset, not_1_out);
  or or_3 (or_3_out, or_1_out, preset);
  not not_2 (not_2_out, clear);
  and and_3 (and_3_out, not_2_out, or_2_out);
  and and_4 (and_4_out, or_3_out, not_3_out);
  not not_3 (not_3_out, clear);
  and and_5 (and_5_out, and_3_out, and_4_out);
endmodule
